# Fritzing sketch Wiring_Diagram (saved by Fritzing 0.9.3b)

parts:
  Part1 = Arduino Uno (Rev3)
  Part2 = ACS712 Low Current Sensor Board v12
  J2 = Basic Servo
  U1 = LIPO-1000mAh [package=lipo-1000]
  Part3 = ACS712 Low Current Sensor Board v12
  C1 = Electrolytic Capacitor [capacitance=220µF voltage=10V package="1010 [SMD, electrolytic]"]  # not connected
  U2 = V_REG MIC5219 [package=sot23-5]
  U3 = V_REG MIC5219 [package=sot23-5]
  J3 = Basic Servo
  C2 = Electrolytic Capacitor [capacitance=220µF voltage=10V package="1010 [SMD, electrolytic]"]  # not connected
  S2 = SWITCH-MOMENTARY-2 [package=tactile-switch-1101ne]
  S3 = SWITCH-MOMENTARY-2 [package=tactile-switch-1101ne]

nets:
  N1: Part1.A0, Part2.VO
  N2: Part1.A1, Part3.VO
  N3: Part1.D8, J3.pulse
  N4: Part1.D9_PWM, J2.pulse
  N5: Part1.GND, U2.BP
  N6: Part1.D2, S3.2
  N7: Part1.D3_PWM, S2.2
  5V: Part1.5V, Part3.5V
  N8: Part1.VIN, U2.OUT
  N9: Part2.IP+, J3.vcc
  GND: Part2.GND, Part3.GND
  N10: J2.vcc, Part3.IP+
  GND_2: U1.+, U2.GND, U3.GND
  N11: U1.-, U2.EN, U3.EN
  N12: Part3.IP-, U3.OUT
  N13: U3.BP, J3.gnd
